# Fritzing sketch temp-humid-lcd (saved by Fritzing 0.9.5d)
circuit board: 8.46667cm x 5.64444cm
breadboards: 1

parts:
  MH-ET_LIVE_ESP32_DEVKIT1 = MH-ET LIVE ESP32 DEVKIT 38 pins
  M1 = HTU21d
  Nokia_5110_LCD_Module1 = Nokia 5110 LCD
  R1 = Resistor [tolerance=±5% resistance=220 package="2010 [SMD]"]

nets:
  3V3: MH-ET_LIVE_ESP32_DEVKIT1.3V3, M1.VIN, Nokia_5110_LCD_Module1.VCC
  N1: MH-ET_LIVE_ESP32_DEVKIT1.IO23, Nokia_5110_LCD_Module1.Din
  N2: MH-ET_LIVE_ESP32_DEVKIT1.IO22, M1.SDA
  N3: MH-ET_LIVE_ESP32_DEVKIT1.IO21, M1.SCL
  GND: MH-ET_LIVE_ESP32_DEVKIT1.GND#70, M1.GND, Nokia_5110_LCD_Module1.GND, R1.Pin_1
  N4: MH-ET_LIVE_ESP32_DEVKIT1.IO19, Nokia_5110_LCD_Module1.RST
  N5: MH-ET_LIVE_ESP32_DEVKIT1.IO18, Nokia_5110_LCD_Module1.CLK
  N6: MH-ET_LIVE_ESP32_DEVKIT1.IO5, Nokia_5110_LCD_Module1.CE
  N7: MH-ET_LIVE_ESP32_DEVKIT1.IO4, Nokia_5110_LCD_Module1.D/C
  N8: Nokia_5110_LCD_Module1.BL, R1.Pin_0

custom parts:
  MH-ET LIVE ESP32 DEVKIT 38 pins: http://mh.nodebb.com/topic/2/mh-et-live-esp32-devkit
  HTU21d: Temperature Humidity Sensor, I2C
  Nokia 5110 LCD: Nokia 5110 Graphic 84*48 LCD module <Blue Version>
